# Fritzing sketch hat (saved by Fritzing 0.9.3b)
breadboards: 1

parts:
  Part1 = Arduino Uno (Rev3)
  J1 = Basic Servo
  J2 = Basic Servo
  J3 = Basic Servo
  VCC1 = 4 x AAA Battery Mount

nets:
  N1: Part1.D9_PWM, J3.pulse
  N2: Part1.D10_PWM/SS, J2.pulse
  N3: Part1.D11_PWM/MOSI, J1.pulse
  GND: Part1.GND, J1.gnd, J2.gnd, J3.gnd, VCC1.-
  VCC: J1.vcc, J2.vcc, J3.vcc, VCC1.+
